// Logisim project braile.circ as structural Verilog: 4 circuits, main circuit main
module main (
  input  b1,
  input  b2,
  input  b3,
  input  b4,
  input  in_5,
  input  in_6,
  input  in_7,
  input  in_8,
  output _1,
  output _4,
  output _2,
  output _5,
  output _3,
  output _6
);

  wire decodificador_de_padroes_de_letras_1_out_5, decodificador_de_padroes_de_letras_1_out_6,
       decodificador_de_padroes_de_letras_1_out_7, decodificador_de_padroes_de_letras_1_out_8,
       decodificador_de_padroes_de_letras_1_out_9, \decodificador_de_padrões_1_out_5 ,
       \decodificador_de_padrões_1_out_6 , \decodificador_de_padrões_1_out_7 ,
       levantador_de_pinos_de_prefixo_1_out_8;

  \decodificador_de_padrões  \decodificador_de_padrões_1  (
    .b1(b1), .b2(b2), .b3(b3), .b4(b4), .out_5(\decodificador_de_padrões_1_out_5 ),
    .out_6(\decodificador_de_padrões_1_out_6 ), .out_7(\decodificador_de_padrões_1_out_7 ));
  levantador_de_pinos_de_prefixo levantador_de_pinos_de_prefixo_1 (
    .in_1(\decodificador_de_padrões_1_out_7 ), .in_2(\decodificador_de_padrões_1_out_6 ),
    .in_3(\decodificador_de_padrões_1_out_5 ), .out_4(_4), .out_5(_6), .out_6(_3), .out_7(_5),
    .out_8(levantador_de_pinos_de_prefixo_1_out_8));
  LED led_1 (.in(levantador_de_pinos_de_prefixo_1_out_8));
  decodificador_de_padroes_de_letras decodificador_de_padroes_de_letras_1 (
    .in_1(in_5), .in_2(in_6), .in_3(in_7), .in_4(in_8), .out_5(decodificador_de_padroes_de_letras_1_out_5),
    .out_6(decodificador_de_padroes_de_letras_1_out_6), .out_7(decodificador_de_padroes_de_letras_1_out_7),
    .out_8(decodificador_de_padroes_de_letras_1_out_8), .out_9(decodificador_de_padroes_de_letras_1_out_9));

  // Notes on the sheet:
  //   lógica para prefixos
  //   levantador de pinos de prefixo
  //   minusculo
  //   pinos
  //   4
  //   6
  //   3
  //   5
  //   pinos
  //   1
  //   2
  //   4
  //   5
  //   3
endmodule

module \decodificador_de_padrões  (
  input  b1,
  input  b2,
  input  b3,
  input  b4,
  output out_5,
  output out_6,
  output out_7
);

  wire and_1_out, and_2_out, and_3_out, and_4_out, and_5_out, and_6_out, and_8_out, and_9_out, and_10_out,
       not_1_out, not_2_out, not_3_out, not_4_out, not_5_out, not_6_out, not_7_out, not_8_out, not_9_out,
       not_10_out, not_11_out, not_12_out, not_13_out, not_14_out, not_15_out, not_16_out, not_17_out,
       or_1_out, or_2_out, or_3_out, or_4_out, or_5_out;

  not not_1 (not_1_out, b1);
  not not_2 (not_2_out, b3);
  not not_3 (not_3_out, b4);
  not not_4 (not_4_out, b1);
  not not_5 (not_5_out, b3);
  not not_6 (not_6_out, b2);
  not not_7 (not_7_out, b3);
  not not_8 (not_8_out, b2);
  not not_9 (not_9_out, b3);
  not not_10 (not_10_out, b4);
  not not_11 (not_11_out, b1);
  not not_12 (not_12_out, b2);
  not not_13 (not_13_out, b2);
  not not_14 (not_14_out, b4);
  not not_15 (not_15_out, b1);
  not not_16 (not_16_out, b4);
  not not_17 (not_17_out, b1);
  and and_1 (and_1_out, not_1_out, b2, not_2_out, not_3_out);
  and and_2 (and_2_out, not_4_out, b2, not_5_out, b4);
  and and_3 (and_3_out, b1, not_6_out, not_7_out, b4);
  and and_4 (and_4_out, b1, not_8_out, b3, b4);
  and and_5 (and_5_out, b1, b2, not_9_out, b4);
  and and_6 (and_6_out, b1, b2, b3, not_10_out);
  and and_7 (out_6, not_11_out, not_12_out, b3, b4);
  and and_8 (and_8_out, b1, not_13_out, b3, not_14_out);
  and and_9 (and_9_out, not_15_out, b2, b3, not_16_out);
  and and_10 (and_10_out, not_17_out, b2, b3, b4);
  or or_1 (or_1_out, and_1_out, and_2_out);
  or or_2 (or_2_out, and_3_out, and_4_out);
  or or_3 (or_3_out, and_5_out, and_6_out);
  or or_4 (or_4_out, and_8_out, and_9_out);
  or or_5 (or_5_out, or_1_out, or_2_out);
  or or_6 (out_5, or_5_out, or_3_out);
  or or_7 (out_7, or_4_out, and_10_out);

  // Notes on the sheet:
  //   Entradas fora do sub
  //   0100 | A - O MAIUSCULO
  //   0101 | P+ MAIUSCULO
  //   1001| É MAIUSCULO
  //   1011| Â À Á MAIUSCULO
  //   1101| Ê Í MAIUSCULO
  //   1110| Ó Ô Ú MAIUSCULO
  //   0011 | 0 - 9
  //   1010 | á í ó ú MINUSCULO
  //   0110 | a - o MINUSCULO
  //   0111 | p+ MINUSCULO
endmodule

module levantador_de_pinos_de_prefixo (
  input  in_1,
  input  in_2,
  input  in_3,
  output out_4,
  output out_5,
  output out_6,
  output out_7,
  output out_8
);

  wire and_1_out, not_1_out, not_2_out, not_3_out, not_4_out, not_5_out, not_6_out, not_7_out;

  not not_1 (not_1_out, in_2);
  not not_2 (not_2_out, in_1);
  not not_3 (not_3_out, in_3);
  not not_4 (not_4_out, in_1);
  not not_5 (not_5_out, in_3);
  not not_6 (not_6_out, in_2);
  and and_1 (and_1_out, in_3, not_1_out, not_2_out);
  and and_2 (out_6, not_3_out, in_2, not_4_out);
  and and_3 (out_8, not_5_out, not_6_out, in_1);
  not not_7 (not_7_out, out_6);
  xnor xnor_1 (out_4, and_1_out, not_7_out);

  assign out_5 = out_4;
  assign out_7 = out_6;

  // Notes on the sheet:
  //   MAIUSCULAS | 46 (M1)
  //   NUMEROS | 3456 (M1)
  //   MINUSCULOS | NENHUM (M1)
endmodule

module decodificador_de_padroes_de_letras (
  input  in_1,
  input  in_2,
  input  in_3,
  input  in_4,
  output out_5,
  output out_6,
  output out_7,
  output out_8,
  output out_9
);

  wire and_1_out, and_2_out, and_3_out, and_4_out, and_5_out, and_6_out, and_7_out, and_8_out, and_9_out,
       and_10_out, and_11_out, and_12_out, and_13_out, and_14_out, and_15_out, not_1_out, not_2_out,
       not_3_out, not_4_out, not_5_out, not_6_out, not_7_out, not_8_out, not_9_out, not_10_out, not_11_out,
       not_12_out, not_13_out, not_14_out, not_15_out, not_16_out, not_17_out, not_18_out, not_19_out,
       not_20_out, not_21_out, not_22_out, not_23_out, not_24_out, not_25_out, not_26_out, not_27_out,
       not_28_out, not_29_out, not_30_out, not_31_out, not_32_out, not_33_out, not_34_out, not_35_out,
       not_36_out, not_37_out, not_38_out, not_39_out, not_40_out, not_41_out, not_42_out, not_43_out,
       not_44_out, not_45_out, not_46_out, not_47_out, not_48_out, not_49_out, not_50_out, not_51_out,
       not_52_out, not_53_out, not_54_out, not_55_out, not_56_out, not_57_out, not_58_out, not_59_out,
       not_60_out, not_61_out, not_62_out, not_63_out, xnor_1_out, xnor_2_out, xnor_3_out, xnor_4_out,
       xnor_5_out, xnor_6_out, xnor_7_out, xnor_8_out, xnor_9_out, xnor_10_out, xnor_11_out, xnor_12_out,
       xnor_13_out, xnor_14_out, xnor_15_out, xnor_16_out, xnor_17_out, xnor_18_out, xnor_19_out,
       xnor_20_out, xnor_21_out, xnor_22_out, xnor_23_out, xnor_25_out, xnor_26_out, xnor_27_out,
       xnor_28_out, xnor_29_out, xnor_31_out, xnor_32_out;

  not not_1 (not_1_out, in_3);
  not not_2 (not_2_out, in_2);
  not not_3 (not_3_out, in_1);
  not not_4 (not_4_out, in_4);
  not not_5 (not_5_out, in_2);
  not not_6 (not_6_out, in_1);
  not not_7 (not_7_out, in_2);
  not not_8 (not_8_out, in_1);
  not not_9 (not_9_out, in_4);
  not not_10 (not_10_out, in_3);
  not not_11 (not_11_out, in_1);
  not not_12 (not_12_out, in_3);
  not not_13 (not_13_out, in_1);
  not not_14 (not_14_out, in_4);
  not not_15 (not_15_out, in_1);
  not not_16 (not_16_out, in_1);
  not not_17 (not_17_out, in_4);
  not not_18 (not_18_out, in_3);
  not not_19 (not_19_out, in_2);
  not not_20 (not_20_out, in_3);
  not not_21 (not_21_out, in_2);
  not not_22 (not_22_out, in_4);
  not not_23 (not_23_out, in_2);
  not not_24 (not_24_out, in_2);
  not not_25 (not_25_out, in_4);
  not not_26 (not_26_out, in_3);
  not not_27 (not_27_out, in_3);
  not not_28 (not_28_out, in_4);
  and and_1 (and_1_out, in_4, not_1_out, not_2_out, not_3_out);
  and and_2 (and_2_out, not_4_out, in_3, not_5_out, not_6_out);
  and and_3 (and_3_out, in_4, in_3, not_7_out, not_8_out);
  and and_4 (and_4_out, not_9_out, not_10_out, in_2, not_11_out);
  and and_5 (and_5_out, in_4, not_12_out, in_2, not_13_out);
  and and_6 (and_6_out, not_14_out, in_3, in_2, not_15_out);
  and and_7 (and_7_out, in_4, in_3, in_2, not_16_out);
  and and_8 (and_8_out, not_17_out, not_18_out, not_19_out, in_1);
  and and_9 (and_9_out, in_4, not_20_out, not_21_out, in_1);
  and and_10 (and_10_out, not_22_out, in_3, not_23_out, in_1);
  and and_11 (and_11_out, in_4, in_3, not_24_out, in_1);
  and and_12 (and_12_out, not_25_out, not_26_out, in_2, in_1);
  and and_13 (and_13_out, in_4, not_27_out, in_2, in_1);
  and and_14 (and_14_out, not_28_out, in_3, in_2, in_1);
  and and_15 (and_15_out, in_4, in_3, in_2, in_1);
  not not_29 (not_29_out, and_2_out);
  xnor xnor_1 (xnor_1_out, and_1_out, not_29_out);
  not not_30 (not_30_out, xnor_1_out);
  xnor xnor_2 (xnor_2_out, not_30_out, and_3_out);
  not not_31 (not_31_out, and_3_out);
  not not_32 (not_32_out, and_4_out);
  not not_33 (not_33_out, xnor_2_out);
  xnor xnor_3 (xnor_3_out, not_31_out, and_4_out);
  xnor xnor_4 (xnor_4_out, not_32_out, and_5_out);
  xnor xnor_5 (xnor_5_out, not_33_out, and_4_out);
  not not_34 (not_34_out, xnor_5_out);
  not not_35 (not_35_out, xnor_6_out);
  xnor xnor_6 (xnor_6_out, not_34_out, and_5_out);
  not not_36 (not_36_out, and_2_out);
  not not_37 (not_37_out, xnor_3_out);
  xnor xnor_7 (xnor_7_out, not_35_out, and_6_out);
  xnor xnor_8 (xnor_8_out, not_36_out, and_6_out);
  xnor xnor_9 (xnor_9_out, not_37_out, and_6_out);
  not not_38 (not_38_out, xnor_7_out);
  not not_39 (not_39_out, xnor_8_out);
  not not_40 (not_40_out, xnor_9_out);
  not not_41 (not_41_out, xnor_4_out);
  xnor xnor_10 (xnor_10_out, not_38_out, and_7_out);
  xnor xnor_11 (xnor_11_out, not_39_out, and_7_out);
  xnor xnor_12 (xnor_12_out, not_40_out, and_7_out);
  xnor xnor_13 (xnor_13_out, not_41_out, and_7_out);
  not not_42 (not_42_out, xnor_10_out);
  not not_43 (not_43_out, xnor_11_out);
  not not_44 (not_44_out, xnor_13_out);
  xnor xnor_14 (xnor_14_out, not_42_out, and_8_out);
  xnor xnor_15 (xnor_15_out, not_43_out, and_8_out);
  not not_45 (not_45_out, xnor_12_out);
  xnor xnor_16 (xnor_16_out, not_44_out, and_8_out);
  not not_46 (not_46_out, xnor_15_out);
  not not_47 (not_47_out, xnor_17_out);
  xnor xnor_17 (xnor_17_out, not_46_out, and_9_out);
  xnor xnor_18 (xnor_18_out, not_45_out, and_9_out);
  xnor xnor_19 (xnor_19_out, not_47_out, and_10_out);
  not not_48 (not_48_out, xnor_18_out);
  not not_49 (not_49_out, xnor_16_out);
  not not_50 (not_50_out, xnor_14_out);
  xnor xnor_20 (xnor_20_out, not_48_out, and_10_out);
  xnor xnor_21 (xnor_21_out, not_49_out, and_10_out);
  xnor xnor_22 (xnor_22_out, not_50_out, and_11_out);
  not not_51 (not_51_out, xnor_22_out);
  not not_52 (not_52_out, xnor_19_out);
  not not_53 (not_53_out, and_11_out);
  xnor xnor_23 (xnor_23_out, not_51_out, and_12_out);
  xnor xnor_24 (out_6, not_52_out, and_12_out);
  xnor xnor_25 (xnor_25_out, not_53_out, and_12_out);
  not not_54 (not_54_out, xnor_23_out);
  not not_55 (not_55_out, xnor_20_out);
  not not_56 (not_56_out, xnor_25_out);
  not not_57 (not_57_out, xnor_26_out);
  xnor xnor_26 (xnor_26_out, not_54_out, and_13_out);
  xnor xnor_27 (xnor_27_out, not_55_out, and_13_out);
  xnor xnor_28 (xnor_28_out, not_56_out, and_13_out);
  xnor xnor_29 (xnor_29_out, not_57_out, and_14_out);
  not not_58 (not_58_out, xnor_27_out);
  not not_59 (not_59_out, xnor_21_out);
  not not_60 (not_60_out, xnor_28_out);
  not not_61 (not_61_out, xnor_29_out);
  xnor xnor_30 (out_7, not_58_out, and_14_out);
  not not_62 (not_62_out, xnor_31_out);
  xnor xnor_31 (xnor_31_out, not_59_out, and_14_out);
  xnor xnor_32 (xnor_32_out, not_60_out, and_14_out);
  xnor xnor_33 (out_5, not_61_out, and_15_out);
  xnor xnor_34 (out_8, not_62_out, and_15_out);
  not not_63 (not_63_out, xnor_32_out);
  xnor xnor_35 (out_9, not_63_out, and_15_out);

  // Notes on the sheet:
  //   A | 1
  //   B | 12
  //   C | 14
  //   D | 145
  //   E | 15
  //   F | 124
  //   G | 1245
  //   H | 125
  //   I | 24
  //   J | 245
  //   K | 13
  //   L | 123
  //   M | 134
  //   N | 1345
  //   O | 135
  //   1
  //   2
  //   4
  //   5
  //   3
  //   pinos
  //   pinos
  //   1
  //   2
  //   4
  //   5
  //   3
endmodule
